# Fritzing sketch 3DPB-Schematic-Episode-02 (saved by Fritzing 0.9.4)

parts:
  Microcontroller = IC, DIP package, 40 pins [chip_label=ATMEGA1284P]
  R1 = Resistor [tolerance=±5% resistance=10k package=THT]
  R2 = Resistor [tolerance=±5% resistance=220 package=THT]
  Power_LED = LED - 3mm [color="Red (635nm)" package="3 mm [THT]"]
  Crystal = Crystal [frequency="16 Mhz" package=SMD]
  C1 = Ceramic Capacitor [capacitance=22pF package="100 mil [THT, multilayer]"]
  C2 = Ceramic Capacitor [capacitance=22pF package="100 mil [THT, multilayer]"]
  R3 = Resistor [tolerance=±5% resistance=220 package=THT]
  Power_LED1 = LED - 3mm [color="Green (565nm)" package="3 mm [THT]"]
  Reset_Switch = Pushbutton [package="[SMD]"]
  C3 = Ceramic Capacitor [capacitance=10nF package="100 mil [THT, multilayer]"]
  ISP = Adafruit AVR 6-ISP Breakout [part_number="AVR 6-ISP"]

nets:
  MOSI: Microcontroller.pin6, ISP.MOSI
  MISO: Microcontroller.pin7, ISP.MISO
  SCK: Microcontroller.pin8, R3.Pin_0, ISP.SCK
  RESET: Microcontroller.pin9, R1.Pin_1, Reset_Switch.Pin_3, Reset_Switch.Pin_4, C3.1, ISP.RST
  5V: Microcontroller.pin10, Microcontroller.pin30, Microcontroller.pin32, R1.Pin_0, R2.Pin_0, ISP.VCC
  GND: Microcontroller.pin11, Microcontroller.pin31, Power_LED.cathode, C1.0, C2.0, Power_LED1.cathode, Reset_Switch.Pin_1, Reset_Switch.Pin_2, C3.0, ISP.GND
  XTAL2: Microcontroller.pin12, Crystal.pin_1, C2.1
  XTAL1: Microcontroller.pin13, Crystal.pin_0, C1.1
  RX: Microcontroller.pin14
  TX: Microcontroller.pin15
  N1: R2.Pin_1, Power_LED.anode
  N2: R3.Pin_1, Power_LED1.anode

notes:
  3D Printer Board - Episode 2, Base circuit diagram for 3D printer main board., 1.0
  Power LED
  Clock
  Reset
  Built-In/Programming Status LED
  Programming Header
  Ground

custom parts:
  Adafruit AVR 6-ISP Breakout: Programming AVR? Always Googling the pinout? Well, now no longer! It's rare to find a mini kit so elegant, it deserves its own Haiku. A simple breakout, 2x3 box header in the center, two 1x3's on the side. Plugs into any breadboard for neat wiring (in both nifty and clean senses of the word). Comes with a quality mini PCB, a 2x3 box header and a small stick of 0.1" header. Requires some light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
