# Fritzing sketch 3DPB-Schematic-Episode-04 (saved by Fritzing 0.9.4)
breadboards: 1

parts:
  C2 = Ceramic Capacitor [capacitance=0.1µF voltage=50V package="100 mil [THT, multilayer]"]
  Microcontroller = IC, DIP package, 40 pins [chip_label=ATMEGA1284P]
  Breakout_Board = IC, DIP package, 16 pins [chip_label=CP2104]

nets:
  RESET: C2.0, Microcontroller.pin9
  N1: C2.1, Breakout_Board.pin2
  RX: Microcontroller.pin14, Breakout_Board.pin4
  TX: Microcontroller.pin15, Breakout_Board.pin3
  5V: Breakout_Board.pin9
  GND: Breakout_Board.pin11

notes:
  USB Interface
  IN
  3D Printer Board - Episode 4, USB port diagram for 3D printer main board., 1.0
