# Fritzing sketch 3DPB-Schemtic-Episode-05 (saved by Fritzing 0.9.4)

parts:
  7805 = Voltage Regulator [package=to220-igo]
  C6 = Ceramic Capacitor [capacitance=0.1µF voltage=50V package="100 mil [THT, multilayer]"]
  C4 = Ceramic Capacitor [capacitance=0.1µF voltage=50V package="100 mil [THT, multilayer]"]
  C3 = Electrolytic Capacitor [capacitance=47µF voltage=50V package="100 mil [THT, electrolytic]"]
  C1 = Electrolytic Capacitor [capacitance=100µF voltage=50V package="100 mil [THT, electrolytic]"]
  Vin_Terminal_Block = Camdenboss CTB0158-2 [part_number=CTB0158-2 package=THT]

nets:
  GND: 7805.GND, C6.0, C4.0, C3.-, C1.-, Vin_Terminal_Block.pin2
  24V/Vin: 7805.IN, C4.1, C3.+, Vin_Terminal_Block.pin1
  5V: C6.1, C1.+

notes:
  3D Printer Board - Episode 5, 5V power regulator circuit diagram for 3D printer main board., 1.0
  5V Power Regulator
  12V/24V
