# Fritzing sketch 3DPB-Schematic-Episode-06 (saved by Fritzing 0.9.4)

parts:
  Microcontroller = IC, DIP package, 40 pins [chip_label=ATMEGA1284P]
  E_Stepper_Motor = Stepper Motor - Bipolar
  E_Driver = Pololu A4988 [package=SO16]
  C1 = Electrolytic Capacitor [capacitance=47µF voltage=50V package="100 mil [THT, electrolytic]"]
  X_Stepper_Motor = Stepper Motor - Bipolar
  X_Driver = Pololu A4988 [package=SO16]
  C2 = Electrolytic Capacitor [capacitance=47µF voltage=50V package="100 mil [THT, electrolytic]"]
  Y_Stepper_Motor = Stepper Motor - Bipolar
  Y_Driver = Pololu A4988 [package=SO16]
  C3 = Electrolytic Capacitor [capacitance=47µF voltage=50V package="100 mil [THT, electrolytic]"]
  Z_Stepper_Motor = Stepper Motor - Bipolar
  Z_Driver = Pololu A4988 [package=SO16]
  C4 = Electrolytic Capacitor [capacitance=47µF voltage=50V package="100 mil [THT, electrolytic]"]

nets:
  E-DIR: Microcontroller.pin1, E_Driver.DIR
  E-STEP: Microcontroller.pin2, E_Driver.STEP
  Z-DIR: Microcontroller.pin3, Z_Driver.DIR
  Z-STEP: Microcontroller.pin4, Z_Driver.STEP
  5V: Microcontroller.pin10, Microcontroller.pin30, Microcontroller.pin32, E_Driver.MS1, E_Driver.MS2, E_Driver.MS3, E_Driver.VDD, X_Driver.MS1, X_Driver.MS2, X_Driver.MS3, X_Driver.VDD, Y_Driver.MS1, Y_Driver.MS2, Y_Driver.MS3, Y_Driver.VDD, Z_Driver.MS1, Z_Driver.MS2, Z_Driver.MS3, Z_Driver.VDD
  GND: Microcontroller.pin11, Microcontroller.pin31, E_Driver.GND, C1.-, X_Driver.GND, C2.-, Y_Driver.GND, C3.-, Z_Driver.GND, C4.-
  XYE-EN: Microcontroller.pin20, E_Driver.ENABLE, X_Driver.ENABLE, Y_Driver.ENABLE
  X-STEP: Microcontroller.pin21, X_Driver.STEP
  X-DIR: Microcontroller.pin27, X_Driver.DIR
  Y-STEP: Microcontroller.pin28, Y_Driver.STEP
  Y-DIR: Microcontroller.pin29
  Z-EN: Microcontroller.pin35, Z_Driver.ENABLE
  N1: E_Stepper_Motor.A, E_Driver.1A
  N2: E_Stepper_Motor.C, E_Driver.2A
  N3: E_Stepper_Motor.B, E_Driver.1B
  N4: E_Stepper_Motor.D, E_Driver.2B
  N5: E_Driver.RESET, E_Driver.SLEEP
  V24: E_Driver.VMOT, C1.+, X_Driver.VMOT, C2.+, Y_Driver.VMOT, C3.+, Z_Driver.VMOT, C4.+
  N6: X_Stepper_Motor.A, X_Driver.1A
  N7: X_Stepper_Motor.C, X_Driver.2A
  N8: X_Stepper_Motor.B, X_Driver.1B
  N9: X_Stepper_Motor.D, X_Driver.2B
  N10: X_Driver.RESET, X_Driver.SLEEP
  N11: Y_Stepper_Motor.A, Y_Driver.1A
  N12: Y_Stepper_Motor.C, Y_Driver.2A
  N13: Y_Stepper_Motor.B, Y_Driver.1B
  N14: Y_Stepper_Motor.D, Y_Driver.2B
  N15: Y_Driver.RESET, Y_Driver.SLEEP
  N16: Z_Stepper_Motor.A, Z_Driver.1A
  N17: Z_Stepper_Motor.C, Z_Driver.2A
  N18: Z_Stepper_Motor.B, Z_Driver.1B
  N19: Z_Stepper_Motor.D, Z_Driver.2B
  N20: Z_Driver.RESET, Z_Driver.SLEEP

notes:
  3D Printer Board - Episode 6, Stepper motor circuit diagram for 3D printer main board., 1.0
