# Fritzing sketch 3DPB-Schematic-Episode-07 (saved by Fritzing 0.9.4)
breadboards: 1

parts:
  Q1 = MOSFET-NCHANNEL [package=to220v]
  R3 = Resistor [tolerance=±5% resistance=10k package=THT]
  JP1 = Header 2 [package=jst-2-pth]
  Q2 = MOSFET-NCHANNEL [package=to220v]
  JP2 = Header 2 [package=jst-2-pth]
  R4 = Resistor [tolerance=±5% resistance=10k package=THT]
  R5 = Resistor [tolerance=±5% resistance=10k package=THT]
  Q3 = MOSFET-NCHANNEL [package=to220v]
  JP3 = Header 2 [package=jst-2-pth]
  Microcontroller = IC, DIP package, 40 pins [chip_label=ATMEGA1284P]

nets:
  BED: Q1.G, R3.Pin_0, Microcontroller.pin18
  N1: Q1.D, JP1.2
  GND: Q1.S, R3.Pin_1, Q2.S, R4.Pin_1, R5.Pin_1, Q3.S, Microcontroller.pin11, Microcontroller.pin31
  Vin: JP1.1, JP2.1, JP3.1
  HOT-END: Q2.G, R4.Pin_0, Microcontroller.pin19
  N2: Q2.D, JP2.2
  FAN1: R5.Pin_0, Q3.G, Microcontroller.pin5
  N3: Q3.D, JP3.2
  5V: Microcontroller.pin10, Microcontroller.pin30, Microcontroller.pin32

notes:
  3D Printer Board - Episode 7, Hot End, Bed and PWM Fan diagram for 3D printer main board., 1.0
  Bed Heater
  Hot End Heater
  Layer Cooling Fan
