# Fritzing sketch 3DPB-Schematic-Episode-08 (saved by Fritzing 0.9.4)
breadboards: 1

parts:
  R1 = Resistor [tolerance=±5% resistance=4.7k package=THT]
  C1 = Electrolytic Capacitor [capacitance=10µF package="100 mil [THT, electrolytic]"]
  T1 = Temperature Sensor (Thermistor) [thermistor_type=NTC package=THT]
  C2 = Electrolytic Capacitor [capacitance=10µF package="100 mil [THT, electrolytic]"]
  R2 = Resistor [tolerance=±5% resistance=4.7k package=THT]
  T2 = Temperature Sensor (Thermistor) [thermistor_type=NTC package=THT]
  Microcontroller = IC, DIP package, 40 pins [chip_label=ATMEGA1284P]

nets:
  5V: R1.Pin_0, R2.Pin_0, Microcontroller.pin10, Microcontroller.pin30, Microcontroller.pin32
  B-TEMP: R1.Pin_1, C1.+, T1.pin_0, Microcontroller.pin34
  GND: C1.-, T1.pin_1, C2.-, T2.pin_1, Microcontroller.pin11, Microcontroller.pin31
  E-TEMP: C2.+, R2.Pin_1, T2.pin_0, Microcontroller.pin33

notes:
  3D Printer Board - Episode 8, Thermistor diagram for 3D printer main board., 1.0
  Bed Temperature
  Hot End Temperature
