# Fritzing sketch 3DPB-Schematic-Episode-09 (saved by Fritzing 0.9.4)
breadboards: 1

parts:
  X_End_Stop_Switch = SWITCH-MOMENTARY-2 [package=tactile-pth]
  R1 = Resistor [tolerance=±5% resistance=10k package=THT]
  R3 = Resistor [tolerance=±5% resistance=10k package=THT]
  Y_End_Stop_Switch = SWITCH-MOMENTARY-2 [package=tactile-pth]
  R5 = Resistor [tolerance=±5% resistance=10k package=THT]
  Z_End_Stop_Switch = SWITCH-MOMENTARY-2 [package=tactile-pth]
  C2 = Ceramic Capacitor [capacitance=10µF package="100 mil [THT, multilayer]"]
  C1 = Ceramic Capacitor [capacitance=10µF package="100 mil [THT, multilayer]"]
  C3 = Ceramic Capacitor [capacitance=10µF package="100 mil [THT, multilayer]"]
  Microcontroller = IC, DIP package, 40 pins [chip_label=ATMEGA1284P]
  R4 = Resistor [tolerance=±5% resistance=470 package=THT]
  LED2 = LED - 5mm [color="Green (565nm)" package="5 mm [THT]"]
  R2 = Resistor [tolerance=±5% resistance=470 package=THT]
  LED1 = LED - 5mm [color="Green (565nm)" package="5 mm [THT]"]
  R6 = Resistor [tolerance=±5% resistance=470 package=THT]
  LED3 = LED - 5mm [color="Green (565nm)" package="5 mm [THT]"]

nets:
  X-STOP: X_End_Stop_Switch.1, R1.Pin_1, C1.0, Microcontroller.pin24, R2.Pin_0
  GND: X_End_Stop_Switch.2, Y_End_Stop_Switch.2, Z_End_Stop_Switch.2, C2.1, C1.1, C3.1, Microcontroller.pin11, Microcontroller.pin31
  5V: R1.Pin_0, R3.Pin_0, R5.Pin_0, Microcontroller.pin10, Microcontroller.pin30, Microcontroller.pin32, LED2.anode, LED1.anode, LED3.anode
  Y-STOP: R3.Pin_1, Y_End_Stop_Switch.1, C2.0, Microcontroller.pin25, R4.Pin_0
  Z-STOP: R5.Pin_1, Z_End_Stop_Switch.1, C3.0, Microcontroller.pin26, R6.Pin_0
  N1: R4.Pin_1, LED2.cathode
  N2: R2.Pin_1, LED1.cathode
  N3: R6.Pin_1, LED3.cathode

notes:
  3D Printer Board - Episode 9, End stop diagram for 3D printer main board., 1.0
  X End Stop
  Y End Stop
  Z End Stop
