# Fritzing sketch 3DPB-Schematic-Episode-10 (saved by Fritzing 0.9.4)

parts:
  Microcontroller = IC, DIP package, 40 pins [chip_label=ATMEGA1284P]
  128x64_LCD = mystery part, 20 pins [chip_label=G12864]
  R1 = Trimmer Potentiometer [maximum_resistance=10kΩ package=THT]

nets:
  5V: Microcontroller.pin10, Microcontroller.pin30, Microcontroller.pin32, 128x64_LCD.pin2, 128x64_LCD.pin19, R1.leg1
  GND: Microcontroller.pin11, Microcontroller.pin31, 128x64_LCD.pin1, 128x64_LCD.pin15, 128x64_LCD.pin20, R1.leg2
  LCD_DAT: Microcontroller.pin23, 128x64_LCD.pin5
  LCD_CS: Microcontroller.pin37, 128x64_LCD.pin4
  LCD_CLK: Microcontroller.pin39, 128x64_LCD.pin6
  N1: 128x64_LCD.pin3, R1.wiper

notes:
  3D Printer Board - Episode 10, LCD diagram for 3D printer main board., 1.0
