# Fritzing sketch 3DPB-Schematic-Episode-11 (saved by Fritzing 0.9.4)

parts:
  Microcontroller = IC, DIP package, 40 pins [chip_label=ATMEGA1284P]
  Piezo_Buzzer = Piezo Speaker
  ENCODER1 = Rotary Encoder with Knob

nets:
  5V: Microcontroller.pin10, Microcontroller.pin30, Microcontroller.pin32, Piezo_Buzzer.pin1
  GND: Microcontroller.pin11, Microcontroller.pin31, ENCODER1.no_name_yet#3, ENCODER1.no_name_yet#5
  ENC_2: Microcontroller.pin16, ENCODER1.no_name_yet#2
  ENC_1: Microcontroller.pin17, ENCODER1.no_name_yet#1
  ENC_BTN: Microcontroller.pin22, ENCODER1.no_name_yet#4
  PIEZO: Microcontroller.pin36, Piezo_Buzzer.pin2

notes:
  3D Printer Board - Episode 11, Encoder and Piezo Buzzer diagram for 3D printer main board., 1.0

custom parts:
  Rotary Encoder with Knob: Rotary Encoder with 1/4" Shaft and Knob
