# Fritzing sketch 3DPB-Schematiic-Episode-12 (saved by Fritzing 0.9.4)
breadboards: 1

parts:
  Part2 = Adafruit MicroSD card breakout board [part_number=MicroSD]
  LED2 = LED - 3mm [color="Green (565nm)" package="3 mm [THT]"]
  R2 = Resistor [tolerance=±5% resistance=220 package="2512 [SMD]"]
  Microcontroller = IC, DIP package, 40 pins [chip_label=ATMEGA1284P]

nets:
  5V: Part2.VCC, LED2.anode, Microcontroller.pin10
  GND: Part2.GND, Microcontroller.pin11
  SCK: Part2.CLK, Microcontroller.pin8
  MISO: Part2.DO, Microcontroller.pin7
  MOSI: Part2.DI, Microcontroller.pin6
  MSD-CS: Part2.CS, Microcontroller.pin40
  N1: Part2.CD, R2.Pin_1
  N2: LED2.cathode, R2.Pin_0

notes:
  3D Printer Board - Episode 12, MicroSD breakout circuit diagram for 3D printer main board., 1.0
  Micro SD Card Interface
  Card Inserted Status Indicator

custom parts:
  Adafruit MicroSD card breakout board: Not just a simple breakout board, this microSD adapter goes the extra mile - designed for ease of use. Onboard 5v->3v regulator provides 150mA for power-hungry cards 3v level shifting means you can use this with ease on either 3v or 5v systems Uses a proper level shifting chip, not resistors: less problems, and faster read/write access Use 3 or 4 digital pins to read and write 2Gb+ of storage!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
